// Digital circuit MAYBACH-SPU-2.1.dig as structural Verilog
module MAYBACH_SPU_2_1 (
  input  clk,
  output [15:0] out_2,
  output [11:0] out_3,
  output [7:0] A,
  output [7:0] B,
  output [7:0] ALU
);

  wire AI, and_1_out, AO, BI, BO, carry, CE, clk_t, CONST, EO, EQL, EXT0, GFXI, HLT, II, J, JI, JO, MC,
       nand_1_out, nand_2_out, nclk, not_1_out, PO, RAMI, RAMO, ROMAO, ROMDO, SU, zero;
  wire [3:0] GFX, reg_inst_1_op;
  wire [7:0] ramdualport_1_d, register_1_q, register_2_q, register_3_q, register_4_q, register_5_q,
       register_6_q, register_7_q, register_8_q, register_9_q, register_10_q, register_11_q, register_12_q,
       register_13_q, register_14_q, register_15_q, register_16_q;
  wire [11:0] ADDR, MEMADDR, reg_inst_1_arg;
  wire [15:0] decoder_1_p;

  DECODER decoder_1 (.GFX(GFX), .P(decoder_1_p));
  and and_1 (and_1_out, clk_t, GFXI);
  Register #(.Bits(8)) register_1 (.D(ALU), .C(and_1_out), .en(decoder_1_p[0]), .Q(register_1_q));
  Register #(.Bits(8)) register_2 (.D(ALU), .C(and_1_out), .en(decoder_1_p[1]), .Q(register_2_q));
  Register #(.Bits(8)) register_3 (.D(ALU), .C(and_1_out), .en(decoder_1_p[2]), .Q(register_3_q));
  Register #(.Bits(8)) register_4 (.D(ALU), .C(and_1_out), .en(decoder_1_p[3]), .Q(register_4_q));
  MAR mar_1 (.ADDR(ADDR), .clk(clk_t), .MC(MC), .MEM(MEMADDR));
  REG_INST reg_inst_1 (.ii(II), .clk(clk_t), .INST(out_2), .ARG(reg_inst_1_arg), .OP(reg_inst_1_op));
  // PC pc_1: pin names not known; wires that end beside it: ADDR, CE, clk_t, J, out_3[10:0]
  Register #(.Bits(8)) register_5 (.D(ALU), .C(and_1_out), .en(decoder_1_p[4]), .Q(register_5_q));
  LED led_1 (.in(register_1_q[0]));
  LED led_2 (.in(register_1_q[1]));
  LED led_3 (.in(register_1_q[2]));
  LED led_4 (.in(register_1_q[3]));
  LED led_5 (.in(register_1_q[4]));
  LED led_6 (.in(register_1_q[5]));
  LED led_7 (.in(register_1_q[6]));
  LED led_8 (.in(register_1_q[7]));
  not not_1 (not_1_out, MEMADDR[11]);
  assign ADDR[0] = CONST ? 1'b0 : 1'bz;  // Driver driver_1
  LED led_9 (.in(register_2_q[0]));
  LED led_10 (.in(register_2_q[1]));
  LED led_11 (.in(register_2_q[2]));
  LED led_12 (.in(register_2_q[3]));
  LED led_13 (.in(register_2_q[4]));
  LED led_14 (.in(register_2_q[5]));
  LED led_15 (.in(register_2_q[6]));
  LED led_16 (.in(register_2_q[7]));
  EEPROM #(.AddrBits(11), .Bits(16)) ROM_A (.A(MEMADDR[10:0]), .CS(not_1_out), .WE(1'b0), .OE(1'b1), .D(out_2));
  Register #(.Bits(8)) register_6 (.D(ALU), .C(and_1_out), .en(decoder_1_p[5]), .Q(register_6_q));
  LED led_17 (.in(register_3_q[0]));
  LED led_18 (.in(register_3_q[1]));
  LED led_19 (.in(register_3_q[2]));
  LED led_20 (.in(register_3_q[3]));
  LED led_21 (.in(register_3_q[4]));
  LED led_22 (.in(register_3_q[5]));
  LED led_23 (.in(register_3_q[6]));
  LED led_24 (.in(register_3_q[7]));
  assign ADDR = PO ? {1'b0, out_3[10:0]} : 12'bz;  // Driver driver_2
  LED led_25 (.in(register_4_q[0]));
  LED led_26 (.in(register_5_q[0]));
  LED led_27 (.in(register_4_q[1]));
  LED led_28 (.in(register_5_q[1]));
  LED led_29 (.in(register_4_q[2]));
  LED led_30 (.in(register_5_q[2]));
  LED led_31 (.in(register_4_q[3]));
  LED led_32 (.in(register_5_q[3]));
  LED led_33 (.in(register_4_q[4]));
  LED led_34 (.in(register_5_q[4]));
  LED led_35 (.in(register_4_q[5]));
  LED led_36 (.in(register_5_q[5]));
  LED led_37 (.in(register_4_q[6]));
  LED led_38 (.in(register_5_q[6]));
  LED led_39 (.in(register_4_q[7]));
  LED led_40 (.in(register_5_q[7]));
  Register #(.Bits(8)) register_7 (.D(ALU), .C(and_1_out), .en(decoder_1_p[6]), .Q(register_7_q));
  LED led_41 (.in(register_6_q[0]));
  LED led_42 (.in(register_6_q[1]));
  LED led_43 (.in(register_6_q[2]));
  LED led_44 (.in(register_6_q[3]));
  LED led_45 (.in(register_6_q[4]));
  LED led_46 (.in(register_6_q[5]));
  LED led_47 (.in(register_6_q[6]));
  LED led_48 (.in(register_6_q[7]));
  assign ALU = ROMDO ? out_2[7:0] : 8'bz;  // Driver driver_3
  // uINST uinst_1: pin names not known; wires that end beside it: reg_inst_1_op, reg_inst_1_arg, nclk, zero, carry, EQL, GFX, CE, J, PO, II, ROMDO, RAMI, RAMO, SU, EO, ALU, BI, ADDR, BO, AI, AO, MC, HLT, GFXI, JI, JO, ROMAO, EXT0
  LED led_49 (.in(register_7_q[0]));
  LED led_50 (.in(register_7_q[1]));
  LED led_51 (.in(register_7_q[2]));
  LED led_52 (.in(register_7_q[3]));
  LED led_53 (.in(register_7_q[4]));
  LED led_54 (.in(register_7_q[5]));
  LED led_55 (.in(register_7_q[6]));
  LED led_56 (.in(register_7_q[7]));
  assign ADDR = ROMAO ? out_2[11:0] : 12'bz;  // Driver driver_4
  Register #(.Bits(8)) register_8 (.D(ALU), .C(and_1_out), .en(decoder_1_p[7]), .Q(register_8_q));
  LED led_57 (.in(register_8_q[0]));
  LED led_58 (.in(register_9_q[0]));
  LED led_59 (.in(register_8_q[1]));
  LED led_60 (.in(register_9_q[1]));
  LED led_61 (.in(register_8_q[2]));
  LED led_62 (.in(register_9_q[2]));
  LED led_63 (.in(register_8_q[3]));
  LED led_64 (.in(register_9_q[3]));
  LED led_65 (.in(register_8_q[4]));
  LED led_66 (.in(register_9_q[4]));
  LED led_67 (.in(register_8_q[5]));
  LED led_68 (.in(register_9_q[5]));
  LED led_69 (.in(register_8_q[6]));
  LED led_70 (.in(register_9_q[6]));
  LED led_71 (.in(register_8_q[7]));
  LED led_72 (.in(register_9_q[7]));
  RAMDualPort #(.AddrBits(4), .Bits(8)) ramdualport_1 (
    .A(MEMADDR[3:0]), .Din(ALU), .str(RAMI), .C(clk_t), .ld(MEMADDR[4]), .D(ramdualport_1_d));
  LED led_73 (.in(register_10_q[0]));
  LED led_74 (.in(register_10_q[1]));
  LED led_75 (.in(register_10_q[2]));
  LED led_76 (.in(register_10_q[3]));
  LED led_77 (.in(register_10_q[4]));
  LED led_78 (.in(register_10_q[5]));
  LED led_79 (.in(register_10_q[6]));
  LED led_80 (.in(register_10_q[7]));
  assign ALU = RAMO ? ramdualport_1_d : 8'bz;  // Driver driver_5
  LED led_81 (.in(register_11_q[0]));
  LED led_82 (.in(register_11_q[1]));
  LED led_83 (.in(register_11_q[2]));
  LED led_84 (.in(register_11_q[3]));
  LED led_85 (.in(register_11_q[4]));
  LED led_86 (.in(register_11_q[5]));
  LED led_87 (.in(register_11_q[6]));
  LED led_88 (.in(register_11_q[7]));
  Register #(.Bits(8)) register_9 (.D(ALU), .C(and_1_out), .en(decoder_1_p[8]), .Q(register_9_q));
  LED led_89 (.in(register_12_q[0]));
  LED led_90 (.in(register_13_q[0]));
  LED led_91 (.in(register_12_q[1]));
  LED led_92 (.in(register_13_q[1]));
  LED led_93 (.in(register_12_q[2]));
  LED led_94 (.in(register_13_q[2]));
  LED led_95 (.in(register_12_q[3]));
  LED led_96 (.in(register_13_q[3]));
  LED led_97 (.in(register_12_q[4]));
  LED led_98 (.in(register_13_q[4]));
  LED led_99 (.in(register_12_q[5]));
  LED led_100 (.in(register_13_q[5]));
  LED led_101 (.in(register_12_q[6]));
  LED led_102 (.in(register_13_q[6]));
  LED led_103 (.in(register_12_q[7]));
  LED led_104 (.in(register_13_q[7]));
  nand nand_1 (nand_1_out, HLT, HLT);
  LED led_105 (.in(register_14_q[0]));
  LED led_106 (.in(register_14_q[1]));
  LED led_107 (.in(register_14_q[2]));
  LED led_108 (.in(register_14_q[3]));
  LED led_109 (.in(register_14_q[4]));
  LED led_110 (.in(register_14_q[5]));
  LED led_111 (.in(register_14_q[6]));
  LED led_112 (.in(register_14_q[7]));
  ALU alu_1 (.A(A), .B(B), .SU(SU), .EO(EO), .out(ALU), .carry(carry), .zero(zero), .EQL(EQL));
  REG_B reg_b_1 (.BUS_i(ALU), .BUS_o(ALU), .clk(clk_t), .BI(BI), .BO(BO), .B(B));
  Register #(.Bits(8)) register_10 (.D(ALU), .C(and_1_out), .en(decoder_1_p[9]), .Q(register_10_q));
  LED led_113 (.in(register_15_q[0]));
  LED led_114 (.in(register_15_q[1]));
  LED led_115 (.in(register_15_q[2]));
  LED led_116 (.in(register_15_q[3]));
  LED led_117 (.in(register_15_q[4]));
  LED led_118 (.in(register_15_q[5]));
  LED led_119 (.in(register_15_q[6]));
  LED led_120 (.in(register_15_q[7]));
  REG_A reg_a_1 (.clk(clk_t), .AI(AI), .AO(AO), .A(A), .BUS_i(ALU), .BUS_o(ALU));
  nand nand_2 (nand_2_out, nand_1_out, clk);
  LED led_121 (.in(register_16_q[0]));
  LED led_122 (.in(register_16_q[1]));
  LED led_123 (.in(register_16_q[2]));
  LED led_124 (.in(register_16_q[3]));
  LED led_125 (.in(register_16_q[4]));
  LED led_126 (.in(register_16_q[5]));
  LED led_127 (.in(register_16_q[6]));
  LED led_128 (.in(register_16_q[7]));
  nand nand_3 (clk_t, nand_2_out, nand_2_out);
  Register #(.Bits(8)) register_11 (.D(ALU), .C(and_1_out), .en(decoder_1_p[10]), .Q(register_11_q));
  nand nand_4 (nclk, clk_t, clk_t);
  Register #(.Bits(8)) register_12 (.D(ALU), .C(and_1_out), .en(decoder_1_p[11]), .Q(register_12_q));
  Register #(.Bits(8)) register_13 (.D(ALU), .C(and_1_out), .en(decoder_1_p[12]), .Q(register_13_q));
  Register #(.Bits(8)) register_14 (.D(ALU), .C(and_1_out), .en(decoder_1_p[13]), .Q(register_14_q));
  Register #(.Bits(8)) register_15 (.D(ALU), .C(and_1_out), .en(decoder_1_p[14]), .Q(register_15_q));
  Register #(.Bits(8)) register_16 (.D(ALU), .C(and_1_out), .en(decoder_1_p[15]), .Q(register_16_q));
  // Pins of 1 and 8 bits meet at MEMADDR[11:4]
  // Pins of 1 and 12 bits meet at ADDR
  // Pins of 1 and 12 bits meet at 12'h800

  assign out_3[11] = 1'b0;

  // Other names for the same wires on the sheet: DATA[7:0] = ALU; IR[15:0] = out_2

  // Notes on the sheet:
  //   clk: Hz: 20
  //   contents of ROM_A (hex, n*v repeats v):
  //   0,a023,a124,a225,a326,a427,0,a528,a629,a72a,a82b,a92c,0,aafa,abfb,acfc,adfd,aefe,
  //   f000,0,0,0,0,0,0,0,0,0,0,0,0,0,0,0,0,0,0,0,0,0,0,0,0,0,0,0,0,0,0,0,0,0,0,0,0,0,0,
  //   0,0,0,0,0,0,0,0,0,0,0,0,0,0,0,0,0,0,0,0,0,0,0,0,0,0,0,0,0,0,0,0,0,0,0,0,0,0,0,0,0,
  //   0,0,0,0,0,0,0,0,0,0,0,0,0,0,0,0,0,0,0,0,0,0,0,0,0,0,0,0,0,0,0,0,0,0,0,0,0,0,0,0,0,
  //   0,0,0,0,0,0,0,0,0,0,0,0,0,0,0,0,0,0,0,0,0,0,0,0,0,0,0,0,0,0,0,0,0,0,0,0,0,0,0,0,0,
  //   0,0,0,0,0,0,0,0,0,0,0,0,0,0,0,0,0,0,0,0,0,0,0,0,0,0,0,0,0,0,0,0,0,0,0,0,0,0,0,0,0,
  //   0,0,0,0,0,0,0,0,0,0,0,0,0,0,0,0,0,0,0,0,0,0,0,0,0,0,0,0,0,0,0,0,0,0,0,0,0,0,0,0,0,
  //   0,0,0,0,0,0,0,0,0,0,0,0,0,0,0,0,0,0,0,0,0,0,0,0,0,0,0,0,0,0,0,0,0,0,0,0,0,0,0,0,0,
  //   0,0,0,0,0,0,0,0,0,0,0,0,0,0,0,0,0,0,0,0,0,0,0,0,0,0,0,0,0,0,0,0,0,0,0,0,0,0,0,0,0,
  //   0,0,0,0,0,0,0,0,0,0,0,0,0,0,0,0,0,0,0,0,0,0,0,0,0,0,0,0,0,0,0,0,0,0,0,0,0,0,0,0,0,
  //   0,0,0,0,0,0,0,0,0,0,0,0,0,0,0,0,0,0,0,0,0,0,0,0,0,0,0,0,0,0,0,0,0,0,0,0,0,0,0,0,0,
  //   0,0,0,0,0,0,0,0,0,0,0,0,0,0,0,0,0,0,0,0,0,0,0,0,0,0,0,0,0,0,0,0,0,0,0,0,0,0,0,0,0,
  //   0,0,0,0,0,0,0,0,0,0,0,0,0,0,0,0,0,0,0,0,0,0,0,0,0,0,0,0,0,0,0,0,0,0,0,0,0,0,0,0,0,
  //   0,0,0,0,0,0,0,0,0,0,0,0,0,0,0,0,0,0,0,0,0,0,0,0,0,0,0,0,0,0,0,0,0,0,0,0,0,0,0,0,0,
  //   0,0,0,0,0,0,0,0,0,0,0,0,0,0,0,0,0,0,0,0,0,0,0,0,0,0,0,0,0,0,0,0,0,0,0,0,0,0,0,0,0,
  //   0,0,0,0,0,0,0,0,0,0,0,0,0,0,0,0,0,0,0,0,0,0,0,0,0,0,0,0,0,0,0,0,0,0,0,0,0,0,0,0,0,
  //   0,0,0,0,0,0,0,0,0,0,0,0,0,0,0,0,0,0,0,0,0,0,0,0,0,0,0,0,0,0,0,0,0,0,0,0,0,0,0,0,0,
  //   0,0,0,0,0,0,0,0,0,0,0,0,0,0,0,0,0,0,0,0,0,0,0,0,0,0,0,0,0,0,0,0,0,0,0,0,0,0,0,0,0,
  //   0,0,0,0,0,0,0,0,0,0,0,0,0,0,0,0,0,0,0,0,0,0,0,0,0,0,0,0,0,0,0,0,0,0,0,0,0,0,0,0,0,
  //   0,0,0,0,0,0,0,0,0,0,0,0,0,0,0,0,0,0,0,0,0,0,0,0,0,0,0,0,0,0,0,0,0,0,0,0,0,0,0,0,0,
  //   0,0,0,0,0,0,0,0,0,0,0,0,0,0,0,0,0,0,0,0,0,0,0,0,0,0,0,0,0,0,0,0,0,0,0,0,0,0,0,0,0,
  //   0,0,0,0,0,0,0,0,0,0,0,0,0,0,0,0,0,0,0,0,0,0,0,0,0,0,0,0,0,0,0,0,0,0,0,0,0,0,0,0,0,
  //   0,0,0,0,0,0,0,0,0,0,0,0,0,0,0,0,0,0,0,0,0,0,0,0,0,0,0,0,0,0,0,0,0,0,0,0,0,0,0,0,0,
  //   0,0,0,0,0,0,0,0,0,0,0,0,0,0,0,0,0,0,0,0,0,0,0,0,0,0,0,0,0,0,0,0,0,0,0,0,0,0,0,0,0,
  //   0,0,0,0,0,0,0,0,0,0,0,0,0,0,0,0,0,0,0,0,0,0,0,0,0,0,0,0,0,0,0,0,0,0,0,0,0,0,0,0,0,
  //   0,0,0,0,0,0,0,0,0,0,0,0,0,0,0,0,0,0,0,0,0,0,0,0,0,0,0,0,0,0,0,0,0,0,0,0,0,0,0,0,0,
  //   0,0,0,0,0,0,0,0,0,0,0,0,0,0,0,0,0,0,0,0,0,0,0,0,0,0,0,0,0,0,0,0,0,0,0,0,0,0,0,0,0,
  //   0,0,0,0,0,0,0,0,0,0,0,0,0,0,0,0,0,0,0,0,0,0,0,0,0,0,0,0,0,0,0,0,0,0,0,0,0,0,0,0,0,
  //   0,0,0,0,0,0,0,0,0,0,0,0,0,0,0,0,0,0,0,0,0,0,0,0,0,0,0,0,0,0,0,0,0,0,0,0,0,0,0,0,0,
  //   0,0,0,0,0,0,0,0,0,0,0,0,0,0,0,0,0,0,0,0,0,0,0,0,0,0,0,0,0,0,0,0,0,0,0,0,0,0,0,0,0,
  //   0,0,0,0,0,0,0,0,0,0,0,0,0,0,0,0,0,0,0,0,0,0,0,0,0,0,0,0,0,0,0,0,0,0,0,0,0,0,0,0,0,
  //   0,0,0,0,0,0,0,0,0,0,0,0,0,0,0,0,0,0,0,0,0,0,0,0,0,0,0,0,0,0,0,0,0,0,0,0,0,0,0,0,0,
  //   0,0,0,0,0,0,0,0,0,0,0,0,0,0,0,0,0,0,0,0,0,0,0,0,0,0,0,0,0,0,0,0,0,0,0,0,0,0,0,0,0,
  //   0,0,0,0,0,0,0,0,0,0,0,0,0,0,0,0,0,0,0,0,0,0,0,0,0,0,0,0,0,0,0,0,0,0,0,0,0,0,0,0,0,
  //   0,0,0,0,0,0,0,0,0,0,0,0,0,0,0,0,0,0,0,0,0,0,0,0,0,0,0,0,0,0,0,0,0,0,0,0,0,0,0,0,0,
  //   0,0,0,0,0,0,0,0,0,0,0,0,0,0,0,0,0,0,0,0,0,0,0,0,0,0,0,0,0,0,0,0,0,0,0,0,0,0,0,0,0,
  //   0,0,0,0,0,0,0,0,0,0,0,0,0,0,0,0,0,0,0,0,0,0,0,0,0,0,0,0,0,0,0,0,0,0,0,0,0,0,0,0,0,
  //   0,0,0,0,0,0,0,0,0,0,0,0,0,0,0,0,0,0,0,0,0,0,0,0,0,0,0,0,0,0,0,0,0,0,0,0,0,0,0,0,0,
  //   0,0,0,0,0,0,0,0,0,0,0,0,0,0,0,0,0,0,0,0,0,0,0,0,0,0,0,0,0,0,0,0,0,0,0,0,0,0,0,0,0,
  //   0,0,0,0,0,0,0,0,0,0,0,0,0,0,0,0,0,0,0,0,0,0,0,0,0,0,0,0,0,0,0,0,0,0,0,0,0,0,0,0,0,
  //   0,0,0,0,0,0,0,0,0,0,0,0,0,0,0,0,0,0,0,0,0,0,0,0,0,0,0,0,0,0,0,0,0,0,0,0,0,0,0,0,0,
  //   0,0,0,0,0,0,0,0,0,0,0,0,0,0,0,0,0,0,0,0,0,0,0,0,0,0,0,0,0,0,0,0,0,0,0,0,0,0,0,0,0,
  //   0,0,0,0,0,0,0,0,0,0,0,0,0,0,0,0,0,0,0,0,0,0,0,0,0,0,0,0,0,0,0,0,0,0,0,0,0,0,0,0,0,
  //   0,0,0,0,0,0,0,0,0,0,0,0,0,0,0,0,0,0,0,0,0,0,0,0,0,0,0,0,0,0,0,0,0,0,0,0,0,0,0,0,0,
  //   0,0,0,0,0,0,0,0,0,0,0,0,0,7e,9,9,9,7f,7f,49,49,49,36,7e,49,49,49,22,7f,41,41,41,3e,
  //   7f,49,49,49,41,7f,9,9,9,1,3e,41,41,51,32,7f,8,8,8,7f,0,41,7e,41,0,30,40,40,41,3f,
  //   7f,8,14,22,41,7f,40,40,40,40,7f,2,4,2,7f,7f,4,8,10,7f,3e,41,41,41,3e,7f,9,9,9,6,3e,
  //   41,51,21,5e,7f,9,9,9,76,26,49,49,49,32,1,1,7f,1,1,3f,40,40,40,3f,1f,20,40,20,1f,3f,
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endmodule
