// Digital circuit PC_TMP.dig as structural Verilog
module PC_TMP (
  input  CE,
  input  clk
);

  wire _74161_1_pin1, _74161_1_pin11, _74161_1_pin12, _74161_1_pin13, _74161_1_pin14, _74161_1_pin15,
       _74161_2_pin11, _74161_2_pin12, _74161_2_pin13, _74161_2_pin14, _74161_2_pin15, _74161_3_pin11,
       _74161_3_pin12, _74161_3_pin13, _74161_3_pin14;

  _74161 _74161_1 (
    .pin1(_74161_1_pin1), .pin2(clk), .pin3(1'b0), .pin4(1'b0), .pin5(1'b0), .pin6(1'b0), .pin7(CE),
    .pin8(1'b0), .pin9(1'b1), .pin10(CE), .pin11(_74161_1_pin11), .pin12(_74161_1_pin12),
    .pin13(_74161_1_pin13), .pin14(_74161_1_pin14), .pin15(_74161_1_pin15), .pin16(1'b1));
  LED led_1 (.in(_74161_1_pin14));
  LED led_2 (.in(_74161_1_pin13));
  LED led_3 (.in(_74161_1_pin12));
  LED led_4 (.in(_74161_1_pin11));
  _74161 _74161_2 (
    .pin1(_74161_1_pin1), .pin2(clk), .pin3(1'b0), .pin4(1'b0), .pin5(1'b0), .pin6(1'b0),
    .pin7(_74161_1_pin15), .pin8(1'b0), .pin9(1'b1), .pin10(_74161_1_pin15), .pin11(_74161_2_pin11),
    .pin12(_74161_2_pin12), .pin13(_74161_2_pin13), .pin14(_74161_2_pin14), .pin15(_74161_2_pin15),
    .pin16(1'b1));
  not not_1 (_74161_1_pin1, _74161_3_pin11);
  LED led_5 (.in(_74161_2_pin14));
  LED led_6 (.in(_74161_2_pin13));
  LED led_7 (.in(_74161_2_pin12));
  LED led_8 (.in(_74161_2_pin11));
  _74161 _74161_3 (
    .pin1(_74161_1_pin1), .pin2(clk), .pin3(1'b0), .pin4(1'b0), .pin5(1'b0), .pin6(1'b0),
    .pin7(_74161_2_pin15), .pin8(1'b0), .pin9(1'b1), .pin10(_74161_2_pin15), .pin11(_74161_3_pin11),
    .pin12(_74161_3_pin12), .pin13(_74161_3_pin13), .pin14(_74161_3_pin14), .pin16(1'b1));  // open: pin15
  LED led_9 (.in(_74161_3_pin14));
  LED led_10 (.in(_74161_3_pin13));
  LED led_11 (.in(_74161_3_pin11));
  LED led_12 (.in(_74161_3_pin12));

  // Notes on the sheet:
  //   clk: Hz: 100
endmodule
