// Digital circuit MAR.dig as structural Verilog
module MAR (
  input  [11:0] ADDR,
  input  MC,
  input  clk,
  output [11:0] MEM
);

  wire [7:4] register_2_q;

  Register #(.Bits(8)) register_1 (.D(ADDR[7:0]), .C(clk), .en(MC), .Q(MEM[7:0]));
  Register #(.Bits(8)) register_2 (.D({4'b0000, ADDR[11:8]}), .C(clk), .en(MC), .Q({register_2_q, MEM[11:8]}));
endmodule
