// Digital circuit REG-B.dig as structural Verilog
module REG_B (
  input  [7:0] BUS_i,
  input  BO,
  input  BI,
  input  clk,
  output [7:0] BUS_o,
  output [7:0] B
);

  LED led_1 (.in(B[7]));
  LED led_2 (.in(B[6]));
  Register #(.Bits(8)) register_1 (.D(BUS_i), .C(clk), .en(BI), .Q(B));
  LED led_3 (.in(B[5]));
  LED led_4 (.in(B[4]));
  LED led_5 (.in(B[3]));
  LED led_6 (.in(B[2]));
  LED led_7 (.in(B[1]));
  LED led_8 (.in(B[0]));
  assign BUS_o = BO ? B : 8'bz;  // Driver driver_1
endmodule
