// Digital circuit REG_INST.dig as structural Verilog
module REG_INST (
  input  ii,
  input  clk,
  input  [15:0] INST,
  output [3:0] OP,
  output [11:0] ARG
);

  Register #(.Bits(8)) register_1 (.D(INST[7:0]), .C(clk), .en(ii), .Q(ARG[7:0]));
  Register #(.Bits(8)) register_2 (.D(INST[15:8]), .C(clk), .en(ii), .Q({OP, ARG[11:8]}));
endmodule
