// Digital circuit fullAdder.dig as structural Verilog
module fullAdder (
  input  A,
  input  B,
  input  C_in,
  output Y,
  output C_out
);

  wire and_1_out, and_2_out, xor_1_out;

  xor xor_1 (xor_1_out, A, B);
  and and_1 (and_1_out, A, B);
  xor xor_2 (Y, xor_1_out, C_in);
  and and_2 (and_2_out, C_in, xor_1_out);
  or or_1 (C_out, and_2_out, and_1_out);
endmodule
