// Digital circuit ALU.dig as structural Verilog
module ALU (
  input  [7:0] A,
  input  [7:0] B,
  input  SU,
  input  EO,
  output [7:0] out,
  output carry,
  output zero,
  output EQL
);

  wire add_2_c_o, and_2_out, and_3_out, nor_1_out, nor_2_out, nor_3_out, nor_4_out, xnor_1_out, xnor_2_out,
       xnor_3_out, xnor_4_out, xnor_5_out, xnor_6_out, xnor_7_out, xnor_8_out;
  wire [3:0] add_1_s, add_2_s, xor_1_out;
  wire [7:4] xor_1_out_2;

  assign {xor_1_out_2, xor_1_out} = B ^ {8{SU}};  // XOr xor_1, 8 bits wide
  xnor xnor_1 (xnor_1_out, A[7], B[7]);
  xnor xnor_2 (xnor_2_out, A[6], B[6]);
  xnor xnor_3 (xnor_3_out, A[5], B[5]);
  xnor xnor_4 (xnor_4_out, A[4], B[4]);
  xnor xnor_5 (xnor_5_out, A[3], B[3]);
  xnor xnor_6 (xnor_6_out, A[2], B[2]);
  xnor xnor_7 (xnor_7_out, A[1], B[1]);
  xnor xnor_8 (xnor_8_out, A[0], B[0]);
  Add #(.Bits(4)) add_1 (.a(A[7:4]), .b(xor_1_out_2), .c_i(add_2_c_o), .s(add_1_s), .c_o(carry));
  and and_1 (EQL, xnor_1_out, xnor_2_out, xnor_3_out, xnor_4_out, xnor_5_out, xnor_6_out, xnor_7_out, xnor_8_out);
  Add #(.Bits(4)) add_2 (.a(A[3:0]), .b(xor_1_out), .c_i(SU), .s(add_2_s), .c_o(add_2_c_o));
  nor nor_1 (nor_1_out, add_2_s[0], add_2_s[1]);
  nor nor_2 (nor_2_out, add_2_s[2], add_2_s[3]);
  nor nor_3 (nor_3_out, add_1_s[0], add_1_s[1]);
  nor nor_4 (nor_4_out, add_1_s[2], add_1_s[3]);
  assign out = EO ? {add_1_s, add_2_s} : 8'bz;  // Driver driver_1
  and and_2 (and_2_out, nor_1_out, nor_2_out);
  and and_3 (and_3_out, nor_3_out, nor_4_out);
  and and_4 (zero, and_2_out, and_3_out);
endmodule
