// Digital circuit DECODER.dig as structural Verilog
module DECODER (
  input  [3:0] GFX,
  output [15:0] P
);

  Decoder #(.Selector_Bits(4)) decoder_1 (
    .sel(GFX), .out_0(P[0]), .out_1(P[1]), .out_2(P[2]), .out_3(P[3]), .out_4(P[4]), .out_5(P[5]),
    .out_6(P[6]), .out_7(P[7]), .out_8(P[8]), .out_9(P[9]), .out_10(P[10]), .out_11(P[11]), .out_12(P[12]),
    .out_13(P[13]), .out_14(P[14]), .out_15(P[15]));
endmodule
