// Digital circuit PC.dig as structural Verilog
module PC (
  input  CE,
  input  clk,
  input  PO,
  input  [11:0] IN,
  input  J,
  output [11:0] OUT
);

  wire [11:0] counterpreset_1_out;

  CounterPreset #(.Bits(12)) counterpreset_1 (
    .en(CE), .C(clk), .dir(1'b0), .in(IN), .ld(J), .clr(1'b0), .out(counterpreset_1_out));  // open: ovf
  assign OUT = PO ? counterpreset_1_out : 12'bz;  // Driver driver_1
endmodule
