// Digital circuit REG-A.dig as structural Verilog
module REG_A (
  input  AI,
  input  [7:0] BUS_i,
  input  AO,
  input  clk,
  output [7:0] BUS_o,
  output [7:0] A
);

  LED led_1 (.in(A[7]));
  LED led_2 (.in(A[6]));
  Register #(.Bits(8)) register_1 (.D(BUS_i), .C(clk), .en(AI), .Q(A));
  LED led_3 (.in(A[5]));
  LED led_4 (.in(A[4]));
  LED led_5 (.in(A[3]));
  LED led_6 (.in(A[2]));
  LED led_7 (.in(A[1]));
  LED led_8 (.in(A[0]));
  assign BUS_o = AO ? A : 8'bz;  // Driver driver_1
endmodule
