// Digital circuit REG-B.dig as structural Verilog
module REG_B (
  input  [7:0] BUS_i,
  input  BO,
  input  BI,
  output [7:0] BUS_o
);

  wire [7:0] register_1_q;

  LED led_1 (.in(register_1_q[7]));
  LED led_2 (.in(register_1_q[6]));
  Register #(.Bits(8)) register_1 (.D(BUS_i), .C(BI), .en(1'b1), .Q(register_1_q));
  LED led_3 (.in(register_1_q[5]));
  LED led_4 (.in(register_1_q[4]));
  LED led_5 (.in(register_1_q[3]));
  LED led_6 (.in(register_1_q[2]));
  LED led_7 (.in(register_1_q[1]));
  LED led_8 (.in(register_1_q[0]));
  assign BUS_o = BO ? register_1_q : 8'bz;  // Driver driver_1
endmodule
