// Digital circuit REG_INST.dig as structural Verilog
module REG_INST (
  input  II,
  input  clk,
  input  [15:0] INST_IN,
  output [3:0] OP_OUT,
  output [11:0] ARG_OUT
);

  Register #(.Bits(8)) register_1 (.D(INST_IN[7:0]), .C(clk), .en(II), .Q(ARG_OUT[7:0]));
  Register #(.Bits(8)) register_2 (.D(INST_IN[15:8]), .C(clk), .en(II), .Q({OP_OUT, ARG_OUT[11:8]}));
endmodule
