// Digital circuit main.dig as structural Verilog
module main (
  input  clk,
  output [15:0] out_2,
  output [11:0] out_3,
  output [7:0] A,
  output [7:0] B,
  output [7:0] ALU
);

  wire AI, and_1_out, AO, BI, BO, carry, CE, clk_t, EO, EQL, EXT0, GFXI, HLT, II, J, JI, JO, MC, nand_1_out,
       nand_2_out, nclk, PO, RAMI, RAMO, ROMAO, ROMDO, SU, zero;
  wire [3:0] GFX, reg_inst_1_op;
  wire [7:0] ramdualport_1_d, register_1_q, register_2_q, register_3_q, register_4_q, register_5_q,
       register_6_q, register_7_q, register_8_q, register_9_q, register_10_q, register_11_q, register_12_q,
       register_13_q, register_14_q, register_15_q, register_16_q;
  wire [11:0] ADDR, MEMADDR, reg_inst_1_arg, REG_JMP_q;
  wire [15:0] decoder_1_p;

  DECODER decoder_1 (.GFX(GFX), .P(decoder_1_p));
  and and_1 (and_1_out, clk_t, GFXI);
  Register #(.Bits(8)) register_1 (.D(ALU), .C(and_1_out), .en(decoder_1_p[0]), .Q(register_1_q));
  // PolarityAwareLED polarityawareled_1: pin names not known; wires that end beside it: register_1_q[0], 1'b0
  // PolarityAwareLED polarityawareled_2: pin names not known; wires that end beside it: register_1_q[1], 1'b0
  // PolarityAwareLED polarityawareled_3: pin names not known; wires that end beside it: register_1_q[2], 1'b0
  // PolarityAwareLED polarityawareled_4: pin names not known; wires that end beside it: register_1_q[3], 1'b0
  // PolarityAwareLED polarityawareled_5: pin names not known; wires that end beside it: register_1_q[4], 1'b0
  // PolarityAwareLED polarityawareled_6: pin names not known; wires that end beside it: register_1_q[5], 1'b0
  // PolarityAwareLED polarityawareled_7: pin names not known; wires that end beside it: register_1_q[6], 1'b0
  // PolarityAwareLED polarityawareled_8: pin names not known; wires that end beside it: register_1_q[7], 1'b0
  Register #(.Bits(8)) register_2 (.D(ALU), .C(and_1_out), .en(decoder_1_p[1]), .Q(register_2_q));
  // PolarityAwareLED polarityawareled_9: pin names not known; wires that end beside it: register_2_q[0], 1'b0
  // PolarityAwareLED polarityawareled_10: pin names not known; wires that end beside it: register_2_q[1], 1'b0
  // PolarityAwareLED polarityawareled_11: pin names not known; wires that end beside it: register_2_q[2], 1'b0
  // PolarityAwareLED polarityawareled_12: pin names not known; wires that end beside it: register_2_q[3], 1'b0
  // PolarityAwareLED polarityawareled_13: pin names not known; wires that end beside it: register_2_q[4], 1'b0
  // PolarityAwareLED polarityawareled_14: pin names not known; wires that end beside it: register_2_q[5], 1'b0
  // PolarityAwareLED polarityawareled_15: pin names not known; wires that end beside it: register_2_q[6], 1'b0
  // PolarityAwareLED polarityawareled_16: pin names not known; wires that end beside it: register_2_q[7], 1'b0
  Register #(.Bits(8)) register_3 (.D(ALU), .C(and_1_out), .en(decoder_1_p[2]), .Q(register_3_q));
  // PolarityAwareLED polarityawareled_17: pin names not known; wires that end beside it: register_3_q[0], 1'b0
  // PolarityAwareLED polarityawareled_18: pin names not known; wires that end beside it: register_3_q[1], 1'b0
  // PolarityAwareLED polarityawareled_19: pin names not known; wires that end beside it: register_3_q[2], 1'b0
  // PolarityAwareLED polarityawareled_20: pin names not known; wires that end beside it: register_3_q[3], 1'b0
  // PolarityAwareLED polarityawareled_21: pin names not known; wires that end beside it: register_3_q[4], 1'b0
  // PolarityAwareLED polarityawareled_22: pin names not known; wires that end beside it: register_3_q[5], 1'b0
  // PolarityAwareLED polarityawareled_23: pin names not known; wires that end beside it: register_3_q[6], 1'b0
  // PolarityAwareLED polarityawareled_24: pin names not known; wires that end beside it: register_3_q[7], 1'b0
  Register #(.Bits(8)) register_4 (.D(ALU), .C(and_1_out), .en(decoder_1_p[3]), .Q(register_4_q));
  MAR mar_1 (.ADDR(ADDR), .clk(clk_t), .MC(MC), .MEM(MEMADDR));
  // PolarityAwareLED polarityawareled_25: pin names not known; wires that end beside it: register_4_q[0], 1'b0
  // PolarityAwareLED polarityawareled_26: pin names not known; wires that end beside it: register_4_q[1], 1'b0
  // PolarityAwareLED polarityawareled_27: pin names not known; wires that end beside it: register_4_q[2], 1'b0
  // PolarityAwareLED polarityawareled_28: pin names not known; wires that end beside it: register_4_q[3], 1'b0
  // PolarityAwareLED polarityawareled_29: pin names not known; wires that end beside it: register_4_q[4], 1'b0
  // PolarityAwareLED polarityawareled_30: pin names not known; wires that end beside it: register_4_q[5], 1'b0
  // PolarityAwareLED polarityawareled_31: pin names not known; wires that end beside it: register_4_q[6], 1'b0
  // PolarityAwareLED polarityawareled_32: pin names not known; wires that end beside it: register_4_q[7], 1'b0
  REG_INST reg_inst_1 (.ii(II), .clk(clk_t), .INST(out_2), .ARG(reg_inst_1_arg), .OP(reg_inst_1_op));
  PC pc_1 (.CE(CE), .clk(clk_t), .J(J), .IN(ADDR), .OUT(out_3[10:0]));
  Register #(.Bits(12)) REG_JMP (.D(ADDR), .C(clk_t), .en(JI), .Q(REG_JMP_q));
  Register #(.Bits(8)) register_5 (.D(ALU), .C(and_1_out), .en(decoder_1_p[4]), .Q(register_5_q));
  // PolarityAwareLED polarityawareled_33: pin names not known; wires that end beside it: register_5_q[0], 1'b0
  // PolarityAwareLED polarityawareled_34: pin names not known; wires that end beside it: register_5_q[1], 1'b0
  // PolarityAwareLED polarityawareled_35: pin names not known; wires that end beside it: register_5_q[2], 1'b0
  // PolarityAwareLED polarityawareled_36: pin names not known; wires that end beside it: register_5_q[3], 1'b0
  // PolarityAwareLED polarityawareled_37: pin names not known; wires that end beside it: register_5_q[4], 1'b0
  // PolarityAwareLED polarityawareled_38: pin names not known; wires that end beside it: register_5_q[5], 1'b0
  // PolarityAwareLED polarityawareled_39: pin names not known; wires that end beside it: register_5_q[6], 1'b0
  // PolarityAwareLED polarityawareled_40: pin names not known; wires that end beside it: register_5_q[7], 1'b0
  assign ADDR = JO ? REG_JMP_q : 12'bz;  // Driver driver_1
  EEPROM #(.AddrBits(11), .Bits(16)) ROM_A (.A(MEMADDR[10:0]), .CS(1'b1), .WE(1'b0), .OE(1'b1), .D(out_2));
  Register #(.Bits(8)) register_6 (.D(ALU), .C(and_1_out), .en(decoder_1_p[5]), .Q(register_6_q));
  // PolarityAwareLED polarityawareled_41: pin names not known; wires that end beside it: register_6_q[0], 1'b0
  // PolarityAwareLED polarityawareled_42: pin names not known; wires that end beside it: register_6_q[1], 1'b0
  // PolarityAwareLED polarityawareled_43: pin names not known; wires that end beside it: register_6_q[2], 1'b0
  // PolarityAwareLED polarityawareled_44: pin names not known; wires that end beside it: register_6_q[3], 1'b0
  // PolarityAwareLED polarityawareled_45: pin names not known; wires that end beside it: register_6_q[4], 1'b0
  // PolarityAwareLED polarityawareled_46: pin names not known; wires that end beside it: register_6_q[5], 1'b0
  // PolarityAwareLED polarityawareled_47: pin names not known; wires that end beside it: register_6_q[6], 1'b0
  // PolarityAwareLED polarityawareled_48: pin names not known; wires that end beside it: register_6_q[7], 1'b0
  assign ADDR = PO ? {1'b0, out_3[10:0]} : 12'bz;  // Driver driver_2
  Register #(.Bits(8)) register_7 (.D(ALU), .C(and_1_out), .en(decoder_1_p[6]), .Q(register_7_q));
  assign ALU = ROMDO ? out_2[7:0] : 8'bz;  // Driver driver_3
  // uINST uinst_1: pin names not known; wires that end beside it: reg_inst_1_op, reg_inst_1_arg, nclk, zero, carry, EQL, GFX, CE, J, PO, II, ROMDO, RAMI, RAMO, SU, EO, ALU, BI, ADDR, BO, AI, AO, MC, HLT, GFXI, JI, JO, ROMAO, EXT0
  // PolarityAwareLED polarityawareled_49: pin names not known; wires that end beside it: register_7_q[0], 1'b0
  // PolarityAwareLED polarityawareled_50: pin names not known; wires that end beside it: register_7_q[1], 1'b0
  // PolarityAwareLED polarityawareled_51: pin names not known; wires that end beside it: register_7_q[2], 1'b0
  // PolarityAwareLED polarityawareled_52: pin names not known; wires that end beside it: register_7_q[3], 1'b0
  // PolarityAwareLED polarityawareled_53: pin names not known; wires that end beside it: register_7_q[4], 1'b0
  // PolarityAwareLED polarityawareled_54: pin names not known; wires that end beside it: register_7_q[5], 1'b0
  // PolarityAwareLED polarityawareled_55: pin names not known; wires that end beside it: register_7_q[6], 1'b0
  // PolarityAwareLED polarityawareled_56: pin names not known; wires that end beside it: register_7_q[7], 1'b0
  assign ADDR = ROMAO ? out_2[11:0] : 12'bz;  // Driver driver_4
  Register #(.Bits(8)) register_8 (.D(ALU), .C(and_1_out), .en(decoder_1_p[7]), .Q(register_8_q));
  RAMDualPort #(.AddrBits(4), .Bits(8)) ramdualport_1 (
    .A(MEMADDR[3:0]), .Din(ALU), .str(RAMI), .C(clk_t), .ld(1'b1), .D(ramdualport_1_d));
  // PolarityAwareLED polarityawareled_57: pin names not known; wires that end beside it: register_8_q[0], 1'b0
  // PolarityAwareLED polarityawareled_58: pin names not known; wires that end beside it: register_8_q[1], 1'b0
  // PolarityAwareLED polarityawareled_59: pin names not known; wires that end beside it: register_8_q[2], 1'b0
  // PolarityAwareLED polarityawareled_60: pin names not known; wires that end beside it: register_8_q[3], 1'b0
  // PolarityAwareLED polarityawareled_61: pin names not known; wires that end beside it: register_8_q[4], 1'b0
  // PolarityAwareLED polarityawareled_62: pin names not known; wires that end beside it: register_8_q[5], 1'b0
  // PolarityAwareLED polarityawareled_63: pin names not known; wires that end beside it: register_8_q[6], 1'b0
  // PolarityAwareLED polarityawareled_64: pin names not known; wires that end beside it: register_8_q[7], 1'b0
  assign ALU = RAMO ? ramdualport_1_d : 8'bz;  // Driver driver_5
  Register #(.Bits(8)) register_9 (.D(ALU), .C(and_1_out), .en(decoder_1_p[8]), .Q(register_9_q));
  // PolarityAwareLED polarityawareled_65: pin names not known; wires that end beside it: register_9_q[0], 1'b0
  // PolarityAwareLED polarityawareled_66: pin names not known; wires that end beside it: register_9_q[1], 1'b0
  // PolarityAwareLED polarityawareled_67: pin names not known; wires that end beside it: register_9_q[2], 1'b0
  // PolarityAwareLED polarityawareled_68: pin names not known; wires that end beside it: register_9_q[3], 1'b0
  // PolarityAwareLED polarityawareled_69: pin names not known; wires that end beside it: register_9_q[4], 1'b0
  // PolarityAwareLED polarityawareled_70: pin names not known; wires that end beside it: register_9_q[5], 1'b0
  // PolarityAwareLED polarityawareled_71: pin names not known; wires that end beside it: register_9_q[6], 1'b0
  // PolarityAwareLED polarityawareled_72: pin names not known; wires that end beside it: register_9_q[7], 1'b0
  nand nand_1 (nand_1_out, HLT, HLT);
  // ALU alu_1: pin names not known; wires that end beside it: A, B, SU, EO, ALU, carry, zero, EQL
  REG_B reg_b_1 (.BUS_i(ALU), .BUS_o(ALU), .clk(clk_t), .BI(BI), .BO(BO), .B(B));
  Register #(.Bits(8)) register_10 (.D(ALU), .C(and_1_out), .en(decoder_1_p[9]), .Q(register_10_q));
  // PolarityAwareLED polarityawareled_73: pin names not known; wires that end beside it: register_10_q[0], 1'b0
  // PolarityAwareLED polarityawareled_74: pin names not known; wires that end beside it: register_10_q[1], 1'b0
  // PolarityAwareLED polarityawareled_75: pin names not known; wires that end beside it: register_10_q[2], 1'b0
  // PolarityAwareLED polarityawareled_76: pin names not known; wires that end beside it: register_10_q[3], 1'b0
  // PolarityAwareLED polarityawareled_77: pin names not known; wires that end beside it: register_10_q[4], 1'b0
  // PolarityAwareLED polarityawareled_78: pin names not known; wires that end beside it: register_10_q[5], 1'b0
  // PolarityAwareLED polarityawareled_79: pin names not known; wires that end beside it: register_10_q[6], 1'b0
  // PolarityAwareLED polarityawareled_80: pin names not known; wires that end beside it: register_10_q[7], 1'b0
  REG_A reg_a_1 (.clk(clk_t), .AI(AI), .AO(AO), .A(A), .BUS_i(ALU), .BUS_o(ALU));
  nand nand_2 (nand_2_out, nand_1_out, clk);
  nand nand_3 (clk_t, nand_2_out, nand_2_out);
  Register #(.Bits(8)) register_11 (.D(ALU), .C(and_1_out), .en(decoder_1_p[10]), .Q(register_11_q));
  // PolarityAwareLED polarityawareled_81: pin names not known; wires that end beside it: register_11_q[0], 1'b0
  // PolarityAwareLED polarityawareled_82: pin names not known; wires that end beside it: register_11_q[1], 1'b0
  // PolarityAwareLED polarityawareled_83: pin names not known; wires that end beside it: register_11_q[2], 1'b0
  // PolarityAwareLED polarityawareled_84: pin names not known; wires that end beside it: register_11_q[3], 1'b0
  // PolarityAwareLED polarityawareled_85: pin names not known; wires that end beside it: register_11_q[4], 1'b0
  // PolarityAwareLED polarityawareled_86: pin names not known; wires that end beside it: register_11_q[5], 1'b0
  // PolarityAwareLED polarityawareled_87: pin names not known; wires that end beside it: register_11_q[6], 1'b0
  // PolarityAwareLED polarityawareled_88: pin names not known; wires that end beside it: register_11_q[7], 1'b0
  nand nand_4 (nclk, clk_t, clk_t);
  Register #(.Bits(8)) register_12 (.D(ALU), .C(and_1_out), .en(decoder_1_p[11]), .Q(register_12_q));
  // PolarityAwareLED polarityawareled_89: pin names not known; wires that end beside it: register_12_q[0], 1'b0
  // PolarityAwareLED polarityawareled_90: pin names not known; wires that end beside it: register_12_q[1], 1'b0
  // PolarityAwareLED polarityawareled_91: pin names not known; wires that end beside it: register_12_q[2], 1'b0
  // PolarityAwareLED polarityawareled_92: pin names not known; wires that end beside it: register_12_q[3], 1'b0
  // PolarityAwareLED polarityawareled_93: pin names not known; wires that end beside it: register_12_q[4], 1'b0
  // PolarityAwareLED polarityawareled_94: pin names not known; wires that end beside it: register_12_q[5], 1'b0
  // PolarityAwareLED polarityawareled_95: pin names not known; wires that end beside it: register_12_q[6], 1'b0
  // PolarityAwareLED polarityawareled_96: pin names not known; wires that end beside it: register_12_q[7], 1'b0
  Register #(.Bits(8)) register_13 (.D(ALU), .C(and_1_out), .en(decoder_1_p[12]), .Q(register_13_q));
  // PolarityAwareLED polarityawareled_97: pin names not known; wires that end beside it: register_13_q[0], 1'b0
  // PolarityAwareLED polarityawareled_98: pin names not known; wires that end beside it: register_13_q[1], 1'b0
  // PolarityAwareLED polarityawareled_99: pin names not known; wires that end beside it: register_13_q[2], 1'b0
  // PolarityAwareLED polarityawareled_100: pin names not known; wires that end beside it: register_13_q[3], 1'b0
  // PolarityAwareLED polarityawareled_101: pin names not known; wires that end beside it: register_13_q[4], 1'b0
  // PolarityAwareLED polarityawareled_102: pin names not known; wires that end beside it: register_13_q[5], 1'b0
  // PolarityAwareLED polarityawareled_103: pin names not known; wires that end beside it: register_13_q[6], 1'b0
  // PolarityAwareLED polarityawareled_104: pin names not known; wires that end beside it: register_13_q[7], 1'b0
  Register #(.Bits(8)) register_14 (.D(ALU), .C(and_1_out), .en(decoder_1_p[13]), .Q(register_14_q));
  // PolarityAwareLED polarityawareled_105: pin names not known; wires that end beside it: register_14_q[0], 1'b0
  // PolarityAwareLED polarityawareled_106: pin names not known; wires that end beside it: register_14_q[1], 1'b0
  // PolarityAwareLED polarityawareled_107: pin names not known; wires that end beside it: register_14_q[2], 1'b0
  // PolarityAwareLED polarityawareled_108: pin names not known; wires that end beside it: register_14_q[3], 1'b0
  // PolarityAwareLED polarityawareled_109: pin names not known; wires that end beside it: register_14_q[4], 1'b0
  // PolarityAwareLED polarityawareled_110: pin names not known; wires that end beside it: register_14_q[5], 1'b0
  // PolarityAwareLED polarityawareled_111: pin names not known; wires that end beside it: register_14_q[6], 1'b0
  // PolarityAwareLED polarityawareled_112: pin names not known; wires that end beside it: register_14_q[7], 1'b0
  Register #(.Bits(8)) register_15 (.D(ALU), .C(and_1_out), .en(decoder_1_p[14]), .Q(register_15_q));
  // PolarityAwareLED polarityawareled_113: pin names not known; wires that end beside it: register_15_q[0], 1'b0
  // PolarityAwareLED polarityawareled_114: pin names not known; wires that end beside it: register_15_q[1], 1'b0
  // PolarityAwareLED polarityawareled_115: pin names not known; wires that end beside it: register_15_q[2], 1'b0
  // PolarityAwareLED polarityawareled_116: pin names not known; wires that end beside it: register_15_q[3], 1'b0
  // PolarityAwareLED polarityawareled_117: pin names not known; wires that end beside it: register_15_q[4], 1'b0
  // PolarityAwareLED polarityawareled_118: pin names not known; wires that end beside it: register_15_q[5], 1'b0
  // PolarityAwareLED polarityawareled_119: pin names not known; wires that end beside it: register_15_q[6], 1'b0
  // PolarityAwareLED polarityawareled_120: pin names not known; wires that end beside it: register_15_q[7], 1'b0
  Register #(.Bits(8)) register_16 (.D(ALU), .C(and_1_out), .en(decoder_1_p[15]), .Q(register_16_q));
  // PolarityAwareLED polarityawareled_121: pin names not known; wires that end beside it: register_16_q[0], 1'b0
  // PolarityAwareLED polarityawareled_122: pin names not known; wires that end beside it: register_16_q[1], 1'b0
  // PolarityAwareLED polarityawareled_123: pin names not known; wires that end beside it: register_16_q[2], 1'b0
  // PolarityAwareLED polarityawareled_124: pin names not known; wires that end beside it: register_16_q[3], 1'b0
  // PolarityAwareLED polarityawareled_125: pin names not known; wires that end beside it: register_16_q[4], 1'b0
  // PolarityAwareLED polarityawareled_126: pin names not known; wires that end beside it: register_16_q[5], 1'b0
  // PolarityAwareLED polarityawareled_127: pin names not known; wires that end beside it: register_16_q[6], 1'b0
  // PolarityAwareLED polarityawareled_128: pin names not known; wires that end beside it: register_16_q[7], 1'b0

  assign out_3[11] = 1'b0;

  // Other names for the same wires on the sheet: DATA[7:0] = ALU; IR[15:0] = out_2

  // Notes on the sheet:
  //   clk: Hz: 20
  //   contents of ROM_A (hex, n*v repeats v):
  //   0000,a023,a124,a225,a326,a427,0000,a528,a629,a72a,a82b,a92c,0000,aafa,abfb,acfc,adfd,aefe,f000,
  //   0000,0000,0000,0000,0000,0000,0000,0000,0000,0000,0000,0000,0000,0000,0000,0000,0000,0000,0000,
  //   0000,0000,0000,0000,0000,0000,0000,0000,0000,0000,0000,0000,0000,0000,0000,0000,0000,0000,0000,
  //   0000,0000,0000,0000,0000,0000,0000,0000,0000,0000,0000,0000,0000,0000,0000,0000,0000,0000,0000,
  //   0000,0000,0000,0000,0000,0000,0000,0000,0000,0000,0000,0000,0000,0000,0000,0000,0000,0000,0000,
  //   0000,0000,0000,0000,0000,0000,0000,0000,0000,0000,0000,0000,0000,0000,0000,0000,0000,0000,0000,
  //   0000,0000,0000,0000,0000,0000,0000,0000,0000,0000,0000,0000,0000,0000,0000,0000,0000,0000,0000,
  //   0000,0000,0000,0000,0000,0000,0000,0000,0000,0000,0000,0000,0000,0000,0000,0000,0000,0000,0000,
  //   0000,0000,0000,0000,0000,0000,0000,0000,0000,0000,0000,0000,0000,0000,0000,0000,0000,0000,0000,
  //   0000,0000,0000,0000,0000,0000,0000,0000,0000,0000,0000,0000,0000,0000,0000,0000,0000,0000,0000,
  //   0000,0000,0000,0000,0000,0000,0000,0000,0000,0000,0000,0000,0000,0000,0000,0000,0000,0000,0000,
  //   0000,0000,0000,0000,0000,0000,0000,0000,0000,0000,0000,0000,0000,0000,0000,0000,0000,0000,0000,
  //   0000,0000,0000,0000,0000,0000,0000,0000,0000,0000,0000,0000,0000,0000,0000,0000,0000,0000,0000,
  //   0000,0000,0000,0000,0000,0000,0000,0000,0000,0000,0000,0000,0000,0000,0000,0000,0000,0000,0000,
  //   0000,0000,0000,0000,0000,0000,0000,0000,0000,0000,0000,0000,0000,0000,0000,0000,0000,0000,0000,
  //   0000,0000,0000,0000,0000,0000,0000,0000,0000,0000,0000,0000,0000,0000,0000,0000,0000,0000,0000,
  //   0000,0000,0000,0000,0000,0000,0000,0000,0000,0000,0000,0000,0000,0000,0000,0000,0000,0000,0000,
  //   0000,0000,0000,0000,0000,0000,0000,0000,0000,0000,0000,0000,0000,0000,0000,0000,0000,0000,0000,
  //   0000,0000,0000,0000,0000,0000,0000,0000,0000,0000,0000,0000,0000,0000,0000,0000,0000,0000,0000,
  //   0000,0000,0000,0000,0000,0000,0000,0000,0000,0000,0000,0000,0000,0000,0000,0000,0000,0000,0000,
  //   0000,0000,0000,0000,0000,0000,0000,0000,0000,0000,0000,0000,0000,0000,0000,0000,0000,0000,0000,
  //   0000,0000,0000,0000,0000,0000,0000,0000,0000,0000,0000,0000,0000,0000,0000,0000,0000,0000,0000,
  //   0000,0000,0000,0000,0000,0000,0000,0000,0000,0000,0000,0000,0000,0000,0000,0000,0000,0000,0000,
  //   0000,0000,0000,0000,0000,0000,0000,0000,0000,0000,0000,0000,0000,0000,0000,0000,0000,0000,0000,
  //   0000,0000,0000,0000,0000,0000,0000,0000,0000,0000,0000,0000,0000,0000,0000,0000,0000,0000,0000,
  //   0000,0000,0000,0000,0000,0000,0000,0000,0000,0000,0000,0000,0000,0000,0000,0000,0000,0000,0000,
  //   0000,0000,0000,0000,0000,0000,0000,0000,0000,0000,0000,0000,0000,0000,0000,0000,0000,0000,0000,
  //   0000,0000,0000,0000,0000,0000,0000,0000,0000,0000,0000,0000,0000,0000,0000,0000,0000,0000,0000,
  //   0000,0000,0000,0000,0000,0000,0000,0000,0000,0000,0000,0000,0000,0000,0000,0000,0000,0000,0000,
  //   0000,0000,0000,0000,0000,0000,0000,0000,0000,0000,0000,0000,0000,0000,0000,0000,0000,0000,0000,
  //   0000,0000,0000,0000,0000,0000,0000,0000,0000,0000,0000,0000,0000,0000,0000,0000,0000,0000,0000,
  //   0000,0000,0000,0000,0000,0000,0000,0000,0000,0000,0000,0000,0000,0000,0000,0000,0000,0000,0000,
  //   0000,0000,0000,0000,0000,0000,0000,0000,0000,0000,0000,0000,0000,0000,0000,0000,0000,0000,0000,
  //   0000,0000,0000,0000,0000,0000,0000,0000,0000,0000,0000,0000,0000,0000,0000,0000,0000,0000,0000,
  //   0000,0000,0000,0000,0000,0000,0000,0000,0000,0000,0000,0000,0000,0000,0000,0000,0000,0000,0000,
  //   0000,0000,0000,0000,0000,0000,0000,0000,0000,0000,0000,0000,0000,0000,0000,0000,0000,0000,0000,
  //   0000,0000,0000,0000,0000,0000,0000,0000,0000,0000,0000,0000,0000,0000,0000,0000,0000,0000,0000,
  //   0000,0000,0000,0000,0000,0000,0000,0000,0000,0000,0000,0000,0000,0000,0000,0000,0000,0000,0000,
  //   0000,0000,0000,0000,0000,0000,0000,0000,0000,0000,0000,0000,0000,0000,0000,0000,0000,0000,0000,
  //   0000,0000,0000,0000,0000,0000,0000,0000,0000,0000,0000,0000,0000,0000,0000,0000,0000,0000,0000,
  //   0000,0000,0000,0000,0000,0000,0000,0000,0000,0000,0000,0000,0000,0000,0000,0000,0000,0000,0000,
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endmodule
